# Fritzing sketch rpi2-car (saved by Fritzing 0.9.3b)

parts:
  S1 = H-Bridge with L298N
  M2 = DC Motor
  M1 = DC Motor
  VCC1 = Battery block 9V  # not connected
  hc-sr1 = hc-sr04
  R2 = Resistor [tolerance=±5% resistance=2.2k package=THT]
  R1 = Resistor [tolerance=±5% resistance=1k package=THT]  # not connected
  Raspberry_Pi1 = Raspberry Pi 2

nets (from the breadboard view):
  5V: S1.5V, hc-sr1.VCC, Raspberry_Pi1.5V
  N1: S1.ENA, S1.ENA-5V
  N2: S1.IN1, Raspberry_Pi1.GIPO18
  N3: S1.IN2, Raspberry_Pi1.GIPO23
  N4: S1.IN3, Raspberry_Pi1.GIPO24
  N5: S1.IN4, Raspberry_Pi1.GIPO25
  N6: S1.ENB, S1.ENB-5V
  N7: S1.M1-01, M2.pin_2
  N8: S1.M1-02, M2.pin_1
  N9: S1.M2-01, M1.pin_1
  N10: S1.M2-02, M1.pin_2
  N11: hc-sr1.Trig, Raspberry_Pi1.GIPO20
  GND: hc-sr1.Echo, hc-sr1.GND, R2.Pin_1, Raspberry_Pi1.GND

custom parts:
  H-Bridge with L298N: h-bridge
